# Fritzing sketch Untitled Sketch (saved by Fritzing 0.9.3b)
breadboards: 1

parts:
  DFRobot_DFPlayer_Mini1 = DFRobot DFPlayer Mini [part_number=DFR0299]
  Componente1 = Arduino Uno (Rev3) - ICSP
  R1 = Resistor [tolerance=±5% resistance=1k package="0402 [SMD]"]
  J1 = Piezo Speaker

nets:
  VCC: DFRobot_DFPlayer_Mini1.VCC, Componente1.5V
  N1: DFRobot_DFPlayer_Mini1.RX, R1.Pin_0
  N2: DFRobot_DFPlayer_Mini1.TX, Componente1.D10_PWM/SS
  N3: DFRobot_DFPlayer_Mini1.SPK_1, J1.pin2
  N4: DFRobot_DFPlayer_Mini1.GND-1, DFRobot_DFPlayer_Mini1.GND-2, Componente1.GND
  N5: DFRobot_DFPlayer_Mini1.SPK_2, J1.pin1
  N6: Componente1.D11_PWM/MOSI, R1.Pin_1
